// Logisim project cpu.circ as structural Verilog: 2 circuits, main circuit main
module main (
  input  [31:0] INSTRUCTION,
  input  CLOCK,
  output [31:0] PROGRAM_COUNTER,
  output [31:0] ra,
  output [31:0] sp,
  output [31:0] t0,
  output [31:0] t1,
  output [31:0] t2,
  output [31:0] s0,
  output [31:0] s1,
  output [31:0] a0
);

  wire DMEM_p1, DMEM_p4;
  wire [2:0] funct3;
  wire [31:0] adder_1_out, Arithmetic_Logic_Unit_result, DMEM_p5, IF_reg, imm_gen_1_out_2,
       RegFile_read_data_1, wb_data;

  Adder #(.width(32)) adder_1 (.a(PROGRAM_COUNTER), .b(32'h4), .out(adder_1_out));  // open: cin, cout
  Register #(.width(32)) PC (.D(adder_1_out), .en(1'b1), .clk(CLOCK), .Q(PROGRAM_COUNTER));  // open: clr
  Register #(.width(32)) register_1 (
    .D(INSTRUCTION), .en(1'b1), .clk(CLOCK), .Q({IF_reg[31:15], funct3, IF_reg[11:0]}));  // open: clr
  regfile_main RegFile (
    .rd(IF_reg[11:7]), .Read_Data_1(RegFile_read_data_1), .ra(ra), .sp(sp), .t0(t0), .t1(t1), .t2(t2),
    .s0(s0), .s1(s1), .a0(a0), .rs1(IF_reg[19:15]), .Write_Data(wb_data), .RegWEn(1'b1), .clk(CLOCK));  // open: rs2, Read_Data_2
  imm_gen imm_gen_1 (.in_1(IF_reg[31:20]), .out_2(imm_gen_1_out_2));
  alu Arithmetic_Logic_Unit (
    .Result(Arithmetic_Logic_Unit_result), .ALUSel(4'b0000), .A(RegFile_read_data_1), .B(imm_gen_1_out_2));
  // mem_main DMEM: pin names not known; wires that end beside it: DMEM_p1, DMEM_p1, CLOCK, DMEM_p4, DMEM_p5
  Multiplexer #(.width(32), .enable("false")) multiplexer_1 (
    .in0(Arithmetic_Logic_Unit_result), .in1(DMEM_p5), .out(wb_data), .sel(1'b0));

  // Other names for the same wires on the sheet: clk = CLOCK; opcode[6:0] = IF_reg[6:0]; rd[4:0] = IF_reg[11:7];
  //   IF_reg[14:12] = funct3; rs1[4:0] = IF_reg[19:15]; imm[11:0] = IF_reg[31:20]

  // Notes on the sheet:
  //   Output
  //   INSTRUCTION DECODE
  //   IF Pipeline Register
  //   IMEM (do **NOT** move this)
  //   Inputs
  //   Inputs/Outputs for testing. Do **NOT** move these.
endmodule

module imm_gen (
  input  [11:0] in_1,
  output [31:0] out_2
);

  assign out_2 = {{20{in_1[11]}}, in_1};  // Bit_Extender bit_extender_1
endmodule
