// Logisim project alu.circ as structural Verilog: 3 circuits, main circuit alu
module alu (
  input  [31:0] A,
  input  [31:0] B,
  input  [3:0] ALUSel,
  output [31:0] Result
);

  wire comparator_1_lt;
  wire [31:0] add0, and1, divu8, mul10, mulh14, mulhu11, or2, remu9, sll6, slt7, sra5, srl4, sub12, xor3;

  Adder #(.width(32)) adder_1 (.a(A), .b(B), .out(add0));  // open: cin, cout
  Adder #(.width(32)) adder_2 (.a(A), .b(B), .out(add0));  // open: cin, cout
  assign and1 = A & B;  // AND_Gate and_1, 32 bits wide
  assign or2 = A | B;  // OR_Gate or_1, 32 bits wide
  assign xor3 = A ^ B;  // XOR_Gate xor_1, 32 bits wide
  Shifter #(.width(32), .shift("lr")) shifter_1 (.in(A), .\dist (B[4:0]), .out(srl4));
  Shifter #(.width(32), .shift("ar")) shifter_2 (.in(A), .\dist (B[4:0]), .out(sra5));
  Shifter #(.width(32)) shifter_3 (.in(A), .\dist (B[4:0]), .out(sll6));
  Comparator #(.width(32)) comparator_1 (.a(A), .b(B), .lt(comparator_1_lt));  // open: gt, eq
  Divider #(.width(32)) divider_1 (.a(A), .b(B), .out(divu8));  // open: upper, rem
  Divider #(.width(32)) divider_2 (.a(A), .b(B), .rem(remu9));  // open: out, upper
  Multiplier #(.width(32)) multiplier_1 (.a(A), .b(B), .out(mul10));  // open: cin, cout
  Multiplier #(.width(32)) multiplier_2 (.a(A), .b(B), .cout(mulhu11));  // open: out, cin
  Subtractor #(.width(32)) subtractor_1 (.a(A), .b(B), .out(sub12));  // open: bin, bout
  mulh mulh_1 (.in_1(A), .in_2(B), .out_3(mulh14));
  Multiplexer #(.width(32), .enable("false")) multiplexer_1 (
    .in0({32{1'b0}}), .in1(32'h1), .out(slt7), .sel(comparator_1_lt));
  Multiplexer #(.select(4), .width(32), .enable("false")) multiplexer_2 (
    .in0(add0), .in1(and1), .in2(or2), .in3(xor3), .in4(srl4), .in5(sra5), .in6(sll6), .in7(slt7),
    .in8(divu8), .in9(remu9), .in10(mul10), .in11(mulhu11), .in12(sub12), .in13(B), .in14(mulh14),
    .out(Result), .sel(ALUSel));  // open: in15

  // Other names for the same wires on the sheet: bsel13[31:0] = B

  // Notes on the sheet:
  //   INPUTS to your circuit
  //   DON'T CHANGE THE LOCATIONS OF THE INPUTS AND OUTPUTS!
  //   OUTPUT from your circuit
endmodule

module test (
);

  alu alu_1 ();  // open: Result, ALUSel, A, B
  alu alu_2 ();  // open: Result, ALUSel, A, B
endmodule

module mulh (
  input  [31:0] in_1,
  input  [31:0] in_2,
  output [31:0] out_3
);

  wire adder_1_cout, or_1_out, subtractor_4_bout;
  wire [31:0] AC, AD, adder_1_out, adder_2_out, BC, BD, im, multiplier_1_cout, multiplier_2_cout,
       multiplier_3_cout, multiplier_4_cout, subtractor_1_out, subtractor_2_out;

  Multiplier #(.width(32)) multiplier_1 (
    .a({in_1[31], {31{1'b0}}}), .b({in_2[31], {31{1'b0}}}), .out(AC), .cout(multiplier_1_cout));  // open: cin
  Multiplier #(.width(32)) multiplier_2 (
    .a({in_1[31], {31{1'b0}}}), .b({1'b0, in_2[30:0]}), .out(AD), .cout(multiplier_2_cout));  // open: cin
  Multiplier #(.width(32)) multiplier_3 (
    .a({1'b0, in_1[30:0]}), .b({in_2[31], {31{1'b0}}}), .out(BC), .cout(multiplier_3_cout));  // open: cin
  Multiplier #(.width(32)) multiplier_4 (
    .a({1'b0, in_1[30:0]}), .b({1'b0, in_2[30:0]}), .out(BD), .cout(multiplier_4_cout));  // open: cin
  Subtractor #(.width(32)) subtractor_1 (
    .a(multiplier_1_cout), .b(multiplier_2_cout), .out(subtractor_1_out));  // open: bin, bout
  Subtractor #(.width(32)) subtractor_2 (
    .a(multiplier_4_cout), .b(multiplier_3_cout), .out(subtractor_2_out));  // open: bin, bout
  Adder #(.width(32)) adder_1 (.a(AD), .b(BC), .out(adder_1_out), .cout(adder_1_cout));  // open: cin
  Adder #(.width(32)) adder_2 (.a(subtractor_1_out), .b(subtractor_2_out), .out(adder_2_out));  // open: cin, cout
  Subtractor #(.width(32)) subtractor_3 (.a(adder_2_out), .b(im), .out(out_3));  // open: bin, bout
  Subtractor #(.width(32)) subtractor_4 (.a(BD), .b(adder_1_out), .bout(subtractor_4_bout));  // open: out, bin
  or or_1 (or_1_out, subtractor_4_bout, adder_1_cout);
  Multiplexer #(.width(32), .enable("false")) multiplexer_1 (.in0({32{1'b0}}), .in1(32'h1), .out(im), .sel(or_1_out));

  // Other names for the same wires on the sheet: A[31] = in_1[31]; B[30:0] = in_1[30:0]; C[31] = in_2[31];
  //   D[30:0] = in_2[30:0]

  // Notes on the sheet:
  //   Design Idea: 32 bit divided into two parts, aka manually do the 2s complement calculation.
  //   (-A + B)(-C + D) = AC - AD - BC - BD
  //   but the lower 32 bit of result still matters, because there will be negtative number that cause the 0 bit in upper part minus 1
  //   So need extra step to calculate -AD - BC + BD to check if the upper bit needs to minus 1 or not
endmodule
